# Fritzing sketch Wiring (saved by Fritzing 1.0.4)
breadboards: 2

parts:
  Bauteil1 = Adafruit TSL2561 [part_number="Adafruit #439"]
  M1 = ESP32-S3-DevKitC-1-N8R8-v1 [part_number=ESP32-S3-DevKitC-1-N8R8-v1]
  Bauteil2 = Adafruit BME680 [part_number="Adafruit #3660"]
  Bauteil3 = Adafruit TSL2561 [part_number="Adafruit #439"]
  Bauteil4 = Adafruit BME680 [part_number="Adafruit #3660"]
  Bauteil5 = Adafruit TSL2561 [part_number="Adafruit #439"]
  Bauteil6 = Adafruit TSL2561 [part_number="Adafruit #439"]
  Bauteil7 = Adafruit BME680 [part_number="Adafruit #3660"]
  Bauteil8 = Adafruit BME680 [part_number="Adafruit #3660"]
  DS1 = DS18B20 1-Wire Temperature Sensor [part_number=DS18B20]
  DS2 = DS18B20 1-Wire Temperature Sensor [part_number=DS18B20]
  DS3 = DS18B20 1-Wire Temperature Sensor [part_number=DS18B20]
  DS4 = DS18B20 1-Wire Temperature Sensor [part_number=DS18B20]
  DS5 = DS18B20 1-Wire Temperature Sensor [part_number=DS18B20]
  DS6 = DS18B20 1-Wire Temperature Sensor [part_number=DS18B20]
  DS7 = DS18B20 1-Wire Temperature Sensor [part_number=DS18B20]
  R1 = Resistor [tolerance=±5% power=0.25W resistance=1k package=THT]
  R2 = Resistor [tolerance=±5% power=0.25W resistance=1k package=THT]
  YL-83_-_Control_Board1 = YL-83 Rain Sensor - Control Board
  YL-83_-_Control_Board2 = YL-83 Rain Sensor - Control Board
  YL-83_-_Control_Board3 = YL-83 Rain Sensor - Control Board
  YL-83_-_Detection_Board1 = YL-83 Rain Sensor - Detection Board
  YL-83_-_Detection_Board2 = YL-83 Rain Sensor - Detection Board
  YL-83_-_Detection_Board3 = YL-83 Rain Sensor - Detection Board

nets:
  VDD: Bauteil1.VIN, M1.pin_1, M1.pin_2, Bauteil2.VCC, Bauteil6.VIN, Bauteil7.VCC, DS1.VDD, DS2.VDD, DS3.VDD, DS4.VDD, DS5.VDD, DS6.VDD, DS7.VDD, R1.Pin_1, R2.Pin_1, YL-83_-_Control_Board1.VCC, YL-83_-_Control_Board2.VCC, YL-83_-_Control_Board3.VCC
  GND: Bauteil1.GND, M1.pin_22, M1.pin_23, M1.pin_24, Bauteil2.GND, Bauteil6.GND, Bauteil7.GND, DS1.GND, DS2.GND, DS3.GND, DS4.GND, DS5.GND, DS6.GND, DS7.GND, YL-83_-_Control_Board1.GND, YL-83_-_Control_Board2.GND, YL-83_-_Control_Board3.GND
  N1: Bauteil1.SDA, M1.pin_5, Bauteil2.SDI/SDA, Bauteil3.SDA, Bauteil4.SDI/SDA
  N2: Bauteil1.SCL, M1.pin_4, Bauteil2.SCK/SCL, Bauteil3.SCL, Bauteil4.SCK/SCL
  N3: M1.pin_6, Bauteil5.SCL, Bauteil6.SCL, Bauteil7.SCK/SCL, Bauteil8.SCK/SCL
  N4: M1.pin_7, Bauteil5.SDA, Bauteil6.SDA, Bauteil7.SDI/SDA, Bauteil8.SDI/SDA
  N5: M1.pin_37, YL-83_-_Control_Board3.DO
  N6: M1.pin_38, YL-83_-_Control_Board2.DO
  N7: M1.pin_39, YL-83_-_Control_Board1.DO
  N8: M1.pin_40, DS5.DQ, DS6.DQ, DS7.DQ, R2.Pin_0
  N9: M1.pin_41, DS1.DQ, DS2.DQ, DS3.DQ, DS4.DQ, R1.Pin_0
  VIN: Bauteil3.VIN, Bauteil4.VCC
  GND_2: Bauteil3.GND, Bauteil3.ADDR, Bauteil4.GND, Bauteil4.SDO/ADR
  VIN_2: Bauteil5.VIN, Bauteil8.VCC
  GND_3: Bauteil5.GND, Bauteil5.ADDR, Bauteil8.GND, Bauteil8.SDO/ADR
  N10: YL-83_-_Control_Board1.POS, YL-83_-_Detection_Board1.POS
  N11: YL-83_-_Control_Board1.NEG, YL-83_-_Detection_Board1.NEG
  N12: YL-83_-_Control_Board2.POS, YL-83_-_Detection_Board2.POS
  N13: YL-83_-_Control_Board2.NEG, YL-83_-_Detection_Board2.NEG
  N14: YL-83_-_Control_Board3.POS, YL-83_-_Detection_Board3.POS
  N15: YL-83_-_Control_Board3.NEG, YL-83_-_Detection_Board3.NEG

notes:
  I2C_0
  I2C_1
  OneWire 1
  OneWire 2

custom parts:
  Adafruit TSL2561: The TSL2561 luminosity sensor is an advanced digital light sensor, ideal for use in a wide range of light situations. Compared to low cost CdS cells, this sensor is more precise, allowing for exact lux calculations and can be configured for different gain/timing ranges to detect light ranges from up to 0.1 - 40,000+ Lux on the fly. The best part of this sensor is that it contains both infrared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
  ESP32-S3-DevKitC-1-N8R8-v1: ESP32-S3-DevKitC-1-N8R8-v1 This module is 44pins long (2x22) and 11 pins width.
  YL-83 Rain Sensor - Control Board: The YL-83 is a rain sensor that has more resistance when dry and less resistance when wet. The module runs at 5V.
  YL-83 Rain Sensor - Detection Board: The YL-83 is a rain sensor that has more resistance when dry and less resistance when wet. The module runs at 5V.
